# Fritzing sketch RaspberryFritzing (saved by Fritzing 0.9.10b)
breadboards: 1

parts:
  Mod1 = Raspberry Pi 4B
  Part1 = ADS1115  # not connected
  M1 = BME680
  Chirp!_Soil_Moisture_Sensor1 = Chirp! Soil Moisture Sensor v2.7.3
  DS1 = DS18B20 1-Wire Temperature Sensor [part_number=DS18B20]
  R3 = Resistor [tolerance=±5% resistance=4.7k package="0603 [SMD]"]

nets:
  N1: Mod1.5V, Mod1.GPIO3, M1.Pin_2, M1.Pin_4, M1.Pin_15, M1.Pin_17, Chirp!_Soil_Moisture_Sensor1.Pin_1
  N2: Mod1.GPIO2, M1.Pin_3
  N3: M1.Pin_1, M1.Pin_18, Chirp!_Soil_Moisture_Sensor1.pin_5
  N4: DS1.VDD, R3.Pin_0, R3.Pin_1

custom parts:
  ADS1115: ADC ADS1115
  BME680: The SparkFun BME680 Environmental Sensor is a breakout that combines a gas sensor with temperature, humidity and barometric pressure sensing for a complete environmental sensor in a single package. The gas sensor on the BME680 can detect a wide variety of volatile organic compounds (or VOC for short) to monitor indoor air quality. Combine that with precise temperature, humidity, and barometric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
